# Fritzing sketch Automacao AU_LCD (saved by Fritzing 0.9.3b)
breadboards: 1

parts:
  DISPLAY = LCD-16X2 [package=lcd-16x2_noholes]
  R1-DIS = Resistor [tolerance=±5% resistance=220 package=THT]
  S-TEMP = Temperature Sensor (Thermistor) [thermistor_type=NTC package=THT]
  R2-TEMP = Resistor [tolerance=±5% resistance=10k package=THT]
  IR-OUT = LED - 3mm [color="Infrared (880nm)" package="3 mm [THT]"]
  R3-IROUT = Resistor [tolerance=±5% resistance=220 package=THT]
  M-RELE = Keyes Relay [package=THT]
  IR-IN = TSOP312.., 314.. [package=THT]
  A-UNO = Arduino Uno (Rev3)

nets (from the schematic view):
  GND: DISPLAY.VO, DISPLAY.R_W, DISPLAY.K, S-TEMP.pin_0, R2-TEMP.Pin_0, R2-TEMP.Pin_1, IR-OUT.anode, M-RELE.ground, IR-IN.GND, A-UNO.A0, A-UNO.GND
  N1: DISPLAY.RS, A-UNO.D2
  N2: DISPLAY.E, A-UNO.D4
  N3: DISPLAY.DB4, A-UNO.D5_PWM
  N4: DISPLAY.DB5, A-UNO.D6_PWM
  N5: DISPLAY.DB6, A-UNO.D7
  N6: DISPLAY.DB7, A-UNO.D8
  N7: DISPLAY.A, R1-DIS.Pin_1
  N8: R1-DIS.Pin_0, M-RELE.power
  N9: IR-OUT.cathode, R3-IROUT.Pin_1
  N10: R3-IROUT.Pin_0, A-UNO.D3_PWM
  N11: M-RELE.signal, A-UNO.D12/MISO
  N12: IR-IN.Data, A-UNO.D11_PWM/MOSI

custom parts:
  Keyes Relay: The Keyes 5V relay module is suitable for SCM development, home appliance control. It uses a 5V~12V TIL control signal which can control DC / AC signal.
